# Fritzing sketch LeonardoKodiIRRemote (saved by Fritzing 0.9.3b)

parts:
  Pro_Micro2 = Pro Micro
  IR_Receiver1 = IR_Receiver

nets:
  GND: Pro_Micro2.GND, IR_Receiver1.GND
  N1: Pro_Micro2.D20/A2, IR_Receiver1.OUT
  VCC: Pro_Micro2.VCC, IR_Receiver1.VCC

custom parts:
  Pro Micro: The SparkFun Pro Micro is a complete USB-based microcontoller development system, in a very small footprint, capable of implementing many types of projects. All programming can be done via the USB port.
  IR_Receiver: 赤外線受信モジュール GP1UXC41QS
